// Logisim project alu-control-Rtype-test.circ as structural Verilog: 1 circuit, main circuit main
module main (
  output [7:0] Test_num,
  output halt,
  output [3:0] Switch
);

  wire clock_1_out;
  wire [5:0] rom_1_data, rom_2_data;
  wire [7:0] adder_1_out;

  Clock clock_1 (.out(clock_1_out));
  Adder adder_1 (.a(8'h1), .b(Test_num), .out(adder_1_out));  // open: cin, cout
  Register register_1 (.D(adder_1_out), .Q(Test_num), .clk(clock_1_out));  // open: en, clr
  Comparator #(.mode("unsigned")) comparator_1 (.a(8'hf), .b(Test_num), .eq(halt));  // open: gt, lt
  ROM #(.dataWidth(6)) rom_1 (.addr(Test_num), .data(rom_1_data));  // open: sel
  ROM #(.dataWidth(6)) rom_2 (.addr(Test_num), .data(rom_2_data));  // open: sel
  // alu_control_main main_1: pin names not known; wires that end beside it: rom_1_data, rom_2_data, Switch

  // Notes on the sheet:
  //   contents of rom_2 (hex, n*v repeats v):
  //   0 2 3 20 21 24 25
  //   funct
  //   opcode (all 0 in R-type)
  //   There should be no blue/red wires here, and the result shouldn't be x's.
endmodule
